# Fritzing sketch infrared (saved by Fritzing 0.9.3b)

parts:
  Part1 = Arduino Uno (Rev3)
  Grove1 = Grove Infrared Emitter

nets:
  N1: Part1.D8, Grove1.TX
  5V: Part1.5V, Grove1.VCC
  GND: Part1.GND, Grove1.GND

notes:
  @iamgoangle
