# Fritzing sketch Sketch (saved by Fritzing 0.9.3b)
breadboards: 1

parts:
  Part1 = Arduino Uno (Rev3)
  R1 = Photocell (LDR) [package=THT]
  R2 = Resistor [tolerance=±5% resistance=4.7 package="1206 [SMD]"]
  R3 = Resistor [tolerance=±5% resistance=4.7 package="2010 [SMD]"]
  LED1 = smd LED [color="Red (633nm)" package="0603 [SMD]"]

nets:
  N1: Part1.A0, R1.pin_1, R3.Pin_0
  N2: Part1.D11_PWM/MOSI, R2.Pin_1
  N3: Part1.5V, R3.Pin_1
  N4: Part1.GND, R1.pin_0, LED1.cathode
  N5: R2.Pin_0, LED1.anode

notes:
  pinmode output
  pinmode input
  4.7Ω
  iamgoangle

// code stored in the sketch: lrd.ino
int ldr = A0;
int led = 11;

void setup()
{
  Serial.begin(9600);
  
  pinMode(ldr, INPUT);
  pinMode(led, OUTPUT);
}

void loop()
{
  int ldrVal = analogRead(ldr);

  Serial.println("LDR Sensor");
  Serial.println(ldrVal);

  if (ldrVal > 400) {
    digitalWrite(led, 255);
  } else {
    digitalWrite(led, 0);
  }

  delay(500);
}
