# Fritzing sketch sketch (saved by Fritzing 0.9.3b)

parts:
  Part1 = KY-015 Temperature & Humidity Sensor Module [package="Breakout board"]
  Part2 = Arduino Uno (Rev3)

nets:
  N1: Part1.S, Part2.5V
  N2: Part1.Vin, Part2.D4
  N3: Part1.-, Part2.GND

notes:
  iamgoangle

custom parts:
  KY-015 Temperature & Humidity Sensor Module: KY-015 temperature and humidity sensor module, provides a low-latency serial interface to measure humidity and temperature.
